// Logisim project Bloque1.circ as structural Verilog: 2 circuits, main circuit Bloque1_jmp
module Bloque1_jmp (
  input  [15:0] register_to_test,
  input  CY,
  input  [7:0] opcode,
  input  [10:0] nxt_address,
  output Preload,
  output [10:0] next_address
);

  wire multiplexer_1_out, not_1_out, or_1_out;

  not not_1 (not_1_out, or_1_out);
  or or_1 (or_1_out, register_to_test[0], register_to_test[1], register_to_test[2], register_to_test[3], register_to_test[4], register_to_test[5], register_to_test[6], register_to_test[7], register_to_test[8], register_to_test[9], register_to_test[10], register_to_test[11], register_to_test[12], register_to_test[13], register_to_test[14], register_to_test[15]);
  Multiplexer #(.select(2), .enable("false")) multiplexer_1 (
    .in0(1'b1), .in1(CY), .in2(register_to_test[15]), .in3(not_1_out), .out(multiplexer_1_out),
    .sel(opcode[5:4]));
  and and_1 (Preload, multiplexer_1_out, opcode[6], ~opcode[7]);  // AND_Gate
  assign next_address = Preload ? nxt_address : 11'bz;  // Controlled_Buffer controlled_buffer_1

  // Notes on the sheet:
  //   jump type:
  //   00: jump always
  //   01: jump if carry
  //   10: jump if negative
  //   11: jump if zero
endmodule

module Bloque1_bsr (
  input  [7:0] opcode,
  input  [10:0] PC,
  input  [10:0] displacement,
  input  CLK,
  output Preload,
  output [10:0] next_address
);

  wire and_1_out, and_2_out;
  wire [10:0] adder_1_out, bit_extender_1_out, return_address_stack_1_tos;

  and and_1 (and_1_out, opcode[4], ~opcode[5], ~opcode[6], ~opcode[7]);  // AND_Gate
  assign bit_extender_1_out = {{1{displacement[9]}}, displacement[9:0]};  // Bit_Extender bit_extender_1
  Adder #(.width(11)) adder_1 (.a(PC), .b(bit_extender_1_out), .out(adder_1_out));  // open: cin, cout
  and and_2 (and_2_out, opcode[0], ~opcode[1], ~opcode[2], ~opcode[3], ~opcode[4], ~opcode[5], ~opcode[6], ~opcode[7]);  // AND_Gate
  return_address_stack return_address_stack_1 (
    .PUSH(and_1_out), .POP(and_2_out), .CLK(CLK), .PC(PC), .TOS(return_address_stack_1_tos));
  assign next_address = and_1_out ? adder_1_out : 11'bz;  // Controlled_Buffer controlled_buffer_1
  assign next_address = and_2_out ? return_address_stack_1_tos : 11'bz;  // Controlled_Buffer controlled_buffer_2
  or or_1 (Preload, and_1_out, and_2_out);

  // Notes on the sheet:
  //   preload para BSR
  //   preload para RET
endmodule
