// Logisim project CLK_MODULE.circ as structural Verilog: 1 circuit, main circuit ClockGenerator
module ClockGenerator (
  input  Auto,
  input  ManualCLK,
  output CLK,
  output CLK2,
  output CLK3,
  output CLK4
);

  wire clock_1_out;

  Clock clock_1 (.out(clock_1_out));
  Multiplexer #(.enable("false")) multiplexer_1 (.in0(ManualCLK), .in1(clock_1_out), .out(CLK), .sel(Auto));

  assign CLK2 = CLK;
  assign CLK3 = CLK;
  assign CLK4 = CLK;
endmodule
