// Logisim project Data_Data.circ as structural Verilog: 1 circuit, main circuit Data
module Data (
  input  [9:0] in_1,
  input  DataWr,
  input  Clk,
  input  [15:0] DataMemInput,
  output [15:0] DataMemOut
);

  wire not_1_out;
  wire [15:0] ram_1_data;

  not not_1 (not_1_out, DataWr);
  RAM #(.addrWidth(10), .dataWidth(16)) ram_1 (.addr(in_1), .we(DataWr), .oe(not_1_out), .clk(Clk), .data(ram_1_data));
  assign ram_1_data = DataWr ? DataMemInput : 16'bz;  // Controlled_Buffer controlled_buffer_1
  assign DataMemOut = not_1_out ? ram_1_data : 16'bz;  // Controlled_Buffer controlled_buffer_2
endmodule
