// Logisim project Data_Data2.circ as structural Verilog: 1 circuit, main circuit Data
module Data (
  input  [9:0] DAddress,
  input  [1:0] M,
  input  clk,
  input  Enable,
  input  [15:0] DataMemInput,
  output [15:0] DataMemOut
);

  wire and_1_out, multiplexer_1_out, not_1_out, not_2_out, xor_1_out;
  wire [15:0] ram_1_data;

  xor xor_1 (xor_1_out, M[0], M[1]);
  and and_1 (and_1_out, xor_1_out, clk, Enable);
  Multiplexer #(.select(2), .enable("false")) multiplexer_1 (
    .in0(1'b0), .in1(1'b1), .in2(1'b0), .in3(1'b0), .out(multiplexer_1_out), .sel(M));
  not not_1 (not_1_out, multiplexer_1_out);
  RAM #(.addrWidth(10), .dataWidth(16)) ram_1 (
    .addr(DAddress), .we(multiplexer_1_out), .oe(not_1_out), .clk(and_1_out), .data(ram_1_data));
  assign ram_1_data = not_2_out ? DataMemInput : 16'bz;  // Controlled_Buffer controlled_buffer_1
  not not_2 (not_2_out, not_1_out);
  assign DataMemOut = not_1_out ? ram_1_data : 16'bz;  // Controlled_Buffer controlled_buffer_2
endmodule
