// Logisim project MicroInstruction_ROM.circ as structural Verilog: 2 circuits, main circuit Micro_Instruction_ROM
module Micro_Instruction_ROM (
  input  [23:0] Instruction,
  output [14:0] MicroInstruction
);

  wire [4:0] instruction_decoder_mic_1_out_2;

  ROM #(.addrWidth(5), .dataWidth(15)) rom_1 (.addr(instruction_decoder_mic_1_out_2), .data(MicroInstruction));
  Instruction_decoder_mic instruction_decoder_mic_1 (.in_1(Instruction), .out_2(instruction_decoder_mic_1_out_2));

  // Notes on the sheet:
  //   contents of rom_1 (hex, n*v repeats v):
  //   0 23 82 41 20 28 21 22 102 102 3903 3903 3103 3103 291b 291b 0 24 5810 6010 1803 203 403 603 281f 0
  //   3 0 3007 0 3807
endmodule

module Instruction_decoder_mic (
  input  [23:0] in_1,
  output [4:0] out_2
);

  wire or_1_out;

  Multiplexer #(.width(4), .enable("false")) multiplexer_1 (
    .in0(in_1[19:16]), .in1(in_1[23:20]), .out(out_2[3:0]), .sel(or_1_out));
  or or_1 (or_1_out, in_1[20], in_1[21], in_1[22], in_1[23]);
  not not_1 (out_2[4], or_1_out);
endmodule
