// Logisim project PIPELINE_pipelineRegister.circ as structural Verilog: 2 circuits, main circuit main
module main (
);

  Pipeline_register pipeline_register_1 ();  // open: ALUC_IN, SH_IN, Kmx_IN, S_low_P_high, CLK, MRyMB_IN, B_bus_IN, T_bus_IN, C_bus_IN, Serial_IN, A_bus_IN, D_Address_IN, Hold, ALUC_OUT, SH_OUT, Kmx_OUT, MRyMB_OUT, B_bus_OUT, T_bus_OUT, C_bus_OUT, Serial_OUT, A_bus_OUT, D_Address_OUT
endmodule

module Pipeline_register (
  input  [3:0] ALUC_IN,
  input  [1:0] SH_IN,
  input  Kmx_IN,
  input  S_low_P_high,
  input  CLK,
  input  [1:0] MRyMB_IN,
  input  [5:0] B_bus_IN,
  input  [5:0] T_bus_IN,
  input  [5:0] C_bus_IN,
  input  [31:0] Serial_IN,
  input  [4:0] A_bus_IN,
  input  [9:0] D_Address_IN,
  input  Hold,
  output [3:0] ALUC_OUT,
  output [1:0] SH_OUT,
  output Kmx_OUT,
  output [1:0] MRyMB_OUT,
  output [5:0] B_bus_OUT,
  output [5:0] T_bus_OUT,
  output [5:0] C_bus_OUT,
  output [31:0] Serial_OUT,
  output [4:0] A_bus_OUT,
  output [9:0] D_Address_OUT
);

  wire multiplexer_2_out, not_1_out;
  wire [1:0] multiplexer_1_out, multiplexer_3_out;
  wire [3:0] multiplexer_8_out;
  wire [4:0] multiplexer_7_out;
  wire [5:0] multiplexer_4_out, multiplexer_5_out, multiplexer_6_out;

  Multiplexer #(.width(2), .enable("false")) multiplexer_1 (
    .in0(Serial_IN[5:4]), .in1(SH_IN), .out(multiplexer_1_out), .sel(S_low_P_high));
  Multiplexer #(.enable("false")) multiplexer_2 (
    .in0(Serial_IN[6]), .in1(Kmx_IN), .out(multiplexer_2_out), .sel(S_low_P_high));
  Multiplexer #(.width(2), .enable("false")) multiplexer_3 (
    .in0(Serial_IN[8:7]), .in1(MRyMB_IN), .out(multiplexer_3_out), .sel(S_low_P_high));
  Multiplexer #(.width(6), .enable("false")) multiplexer_4 (
    .in0(Serial_IN[14:9]), .in1(B_bus_IN), .out(multiplexer_4_out), .sel(S_low_P_high));
  Multiplexer #(.width(6), .enable("false")) multiplexer_5 (
    .in0(Serial_IN[20:15]), .in1(T_bus_IN), .out(multiplexer_5_out), .sel(S_low_P_high));
  Multiplexer #(.width(6), .enable("false")) multiplexer_6 (
    .in0(Serial_IN[26:21]), .in1(C_bus_IN), .out(multiplexer_6_out), .sel(S_low_P_high));
  Multiplexer #(.width(5), .enable("false")) multiplexer_7 (
    .in0(Serial_IN[31:27]), .in1(A_bus_IN), .out(multiplexer_7_out), .sel(S_low_P_high));
  Multiplexer #(.width(4), .enable("false")) multiplexer_8 (
    .in0(Serial_IN[3:0]), .in1(ALUC_IN), .out(multiplexer_8_out), .sel(S_low_P_high));
  not not_1 (not_1_out, Hold);
  Register #(.width(4), .trigger("falling")) ALUC (
    .D(multiplexer_8_out), .en(not_1_out), .clk(CLK), .Q(ALUC_OUT));  // open: clr
  Register #(.width(2), .trigger("falling")) SH (
    .D(multiplexer_1_out), .en(not_1_out), .clk(CLK), .Q(Serial_OUT[5:4]));  // open: clr
  Register #(.width(1), .trigger("falling")) Kmx (
    .D(multiplexer_2_out), .en(not_1_out), .clk(CLK), .Q(Kmx_OUT));  // open: clr
  Register #(.width(2), .trigger("falling")) MRyMB (
    .D(multiplexer_3_out), .en(not_1_out), .clk(CLK), .Q(MRyMB_OUT));  // open: clr
  Register #(.width(6), .trigger("falling")) Bbus (
    .D(multiplexer_4_out), .en(not_1_out), .clk(CLK), .Q(B_bus_OUT));  // open: clr
  Register #(.width(6), .trigger("falling")) Tbus (
    .D(multiplexer_5_out), .en(not_1_out), .clk(CLK), .Q(Serial_OUT[20:15]));  // open: clr
  Register #(.width(6), .trigger("falling")) Cbus (
    .D(multiplexer_6_out), .en(not_1_out), .clk(CLK), .Q(C_bus_OUT));  // open: clr
  Register #(.width(5), .trigger("falling")) Abus (
    .D(multiplexer_7_out), .en(not_1_out), .clk(CLK), .Q(A_bus_OUT));  // open: clr
  Register #(.width(10), .trigger("falling")) DAddr (
    .D(D_Address_IN), .en(not_1_out), .clk(CLK), .Q(D_Address_OUT));  // open: clr

  assign {Serial_OUT[31:21], Serial_OUT[14:6], Serial_OUT[3:0]} = {A_bus_OUT, C_bus_OUT, B_bus_OUT, MRyMB_OUT, Kmx_OUT, ALUC_OUT};
  assign SH_OUT = Serial_OUT[5:4];
  assign T_bus_OUT = Serial_OUT[20:15];

  // Other names for the same wires on the sheet: ALUC_IN_t[3:0] = Serial_IN[3:0]; SH_IN_t[1:0] = Serial_IN[5:4];
  //   Kmx_IN_t = Serial_IN[6]; MRyMB_IN_t[1:0] = Serial_IN[8:7]; B_bus_IN_t[5:0] = Serial_IN[14:9];
  //   T_bus_IN_t[5:0] = Serial_IN[20:15]; C_bus_IN_t[5:0] = Serial_IN[26:21]; A_bus_IN_t[4:0] = Serial_IN[31:27];
  //   Serial_Paralel = S_low_P_high
endmodule
