// Logisim project Selector_A.circ as structural Verilog: 1 circuit, main circuit Selector_A
module Selector_A (
  input  [23:0] BusB,
  output [5:0] BusASel
);

  wire and_1_out, and_2_out, and_3_out, and_4_out, and_5_out, and_6_out, not_1_out, or_1_out, or_2_out,
       or_3_out;

  or or_1 (or_1_out, BusB[16], BusB[17]);
  and and_1 (and_1_out, BusB[20], BusB[21], ~BusB[22], ~BusB[23]);  // AND_Gate
  and and_2 (and_2_out, BusB[18], BusB[19], ~BusB[23]);  // AND_Gate
  and and_3 (and_3_out, or_1_out, BusB[18], ~BusB[19], ~BusB[23]);  // AND_Gate
  and and_4 (and_4_out, BusB[17], BusB[19], ~BusB[18], ~BusB[23]);  // AND_Gate
  and and_5 (and_5_out, ~BusB[17], BusB[19], ~BusB[18], ~BusB[23]);  // AND_Gate
  and and_6 (and_6_out, BusB[21], BusB[22], ~BusB[23]);  // AND_Gate
  or or_2 (or_2_out, and_1_out, and_2_out, and_3_out);
  assign BusASel = and_6_out ? {1'b1, BusB[4:0]} : 6'bz;  // Controlled_Buffer controlled_buffer_1
  assign BusASel = or_2_out ? {1'b1, BusB[4:0]} : 6'bz;  // Controlled_Buffer controlled_buffer_2
  assign BusASel = and_4_out ? {1'b1, BusB[9:5]} : 6'bz;  // Controlled_Buffer controlled_buffer_3
  assign BusASel = and_5_out ? {1'b1, BusB[14:10]} : 6'bz;  // Controlled_Buffer controlled_buffer_4
  assign BusASel = not_1_out ? {6{1'b0}} : 6'bz;  // Controlled_Buffer controlled_buffer_5
  or or_3 (or_3_out, or_2_out, and_4_out, and_5_out, and_6_out);
  not not_1 (not_1_out, or_3_out);
endmodule
