// Logisim project Selector_B_.circ as structural Verilog: 1 circuit, main circuit Selector_B
module Selector_B (
  input  [23:0] in_1,
  output [5:0] out_2
);

  wire and_1_out, and_2_out, and_3_out, and_4_out, and_5_out, and_6_out, and_7_out, nor_1_out, or_1_out,
       or_2_out;

  and and_1 (and_1_out, in_1[21], ~in_1[22], in_1[23]);  // AND_Gate
  and and_2 (and_2_out, ~in_1[21], in_1[22], in_1[23]);  // AND_Gate
  and and_3 (and_3_out, in_1[21], in_1[22], in_1[23]);
  and and_4 (and_4_out, ~in_1[16], ~in_1[17], in_1[18], ~in_1[19], ~in_1[23]);  // AND_Gate
  and and_5 (and_5_out, ~in_1[17], ~in_1[18], in_1[19], ~in_1[23]);  // AND_Gate
  and and_6 (and_6_out, ~in_1[17], in_1[18], in_1[19], ~in_1[23]);  // AND_Gate
  and and_7 (and_7_out, in_1[17], in_1[18], in_1[19], ~in_1[23]);  // AND_Gate
  assign out_2 = or_1_out ? {1'b0, in_1[4:0]} : 6'bz;  // Controlled_Buffer controlled_buffer_1
  or or_1 (or_1_out, and_1_out, and_2_out, and_3_out, and_4_out);
  assign out_2 = or_2_out ? {1'b0, in_1[9:5]} : 6'bz;  // Controlled_Buffer controlled_buffer_2
  or or_2 (or_2_out, and_5_out, and_6_out, and_7_out);
  assign out_2 = nor_1_out ? 6'b100000 : 6'bz;  // Controlled_Buffer controlled_buffer_3
  nor nor_1 (nor_1_out, or_1_out, or_2_out);
endmodule
