// Logisim project Selector_C.circ as structural Verilog: 1 circuit, main circuit Selector_C
module Selector_C (
  input  [23:0] BusB,
  output [5:0] BusC_Selector
);

  wire and_1_out, and_2_out, or_1_out, or_2_out, or_3_out;

  and and_1 (and_1_out, ~BusB[20], BusB[21]);  // AND_Gate
  or or_1 (or_1_out, BusB[18], BusB[19]);
  or or_2 (or_2_out, or_1_out, and_1_out);
  and and_2 (and_2_out, or_2_out, ~BusB[23]);  // AND_Gate
  or or_3 (or_3_out, and_2_out, BusB[23]);
  Multiplexer #(.width(6), .enable("false")) multiplexer_1 (
    .in0({6{1'b0}}), .in1({1'b1, BusB[4:0]}), .out(BusC_Selector), .sel(or_3_out));
endmodule
