// Logisim project Selector_K.circ as structural Verilog: 2 circuits, main circuit selector_K
module selector_K (
  input  [23:0] instruction_register,
  output [15:0] constante_K
);


  assign constante_K = instruction_register[20:5];
endmodule

module Selector_D (
  input  [23:0] instruction_register,
  output [9:0] D_address
);


  assign D_address = instruction_register[14:5];
endmodule
