// Logisim project UC1.circ as structural Verilog: 1 circuit, main circuit UC1
module UC1 (
  input  HOLD,
  input  [31:0] Serial_IN,
  input  [9:0] DAddress_IN,
  output ALUEnable,
  output LoadStoreEnable,
  output [31:0] Serial_ALU_OUT,
  output [31:0] Serial_Load_OUT,
  output [9:0] DAddress_ALU_OUT,
  output [9:0] DAddress_Load_OUT
);

  wire not_1_out, or_1_out;

  or or_1 (or_1_out, Serial_IN[7], Serial_IN[8]);
  not not_1 (not_1_out, or_1_out);
  Multiplexer #(.enable("false")) multiplexer_1 (.in0(not_1_out), .in1(1'b0), .out(ALUEnable), .sel(HOLD));
  Multiplexer #(.enable("false")) multiplexer_2 (.in0(or_1_out), .in1(1'b0), .out(LoadStoreEnable), .sel(HOLD));
  Demultiplexer #(.width(32), .enable("false")) demultiplexer_1 (
    .out0(Serial_ALU_OUT), .out1(Serial_Load_OUT), .in(Serial_IN), .sel(or_1_out));
  Demultiplexer #(.width(10), .enable("false")) demultiplexer_2 (
    .out0(DAddress_ALU_OUT), .out1(DAddress_Load_OUT), .in(DAddress_IN), .sel(or_1_out));
endmodule
