// Logisim project instruction2registerSelector.circ as structural Verilog: 1 circuit, main circuit instruction2register
module instruction2register (
  input  [23:0] Instruction,
  output [9:0] Daddresss,
  output [5:0] A,
  output [5:0] B,
  output [5:0] C,
  output [15:0] K
);

  Selector_A selector_a_1 (.BusB(Instruction), .BusASel(A));
  Selector_B selector_b_1 (.in_1(Instruction), .out_2(B));
  Selector_C selector_c_1 (.BusB(Instruction), .BusC_Selector(C));
  Selector_D selector_d_1 (.instruction_register(Instruction), .D_address(Daddresss));
  selector_K selector_k_1 (.instruction_register(Instruction), .constante_K(K));
endmodule
