// Logisim project judge_judge.circ as structural Verilog: 1 circuit, main circuit judge
module judge (
  input  [14:0] reg_in_alu,
  input  [14:0] reg_in_memory,
  input  [5:0] A_alu,
  input  [5:0] A_mem,
  input  [5:0] B_alu,
  input  [5:0] B_mem,
  input  [5:0] C_alu,
  input  [5:0] C_mem,
  input  [1:0] in_9,
  output [14:0] reg_out,
  output [5:0] A_bus,
  output [5:0] B_bus,
  output [5:0] C_bus
);

  Multiplexer #(.select(2), .width(15), .enable("false")) multiplexer_1 (
    .in0({15{1'b0}}), .in1(reg_in_alu), .in2(reg_in_memory), .in3(reg_in_memory), .out(reg_out), .sel(in_9));
  Multiplexer #(.select(2), .width(6), .enable("false")) multiplexer_2 (
    .in0({6{1'b0}}), .in1(A_alu), .in2(A_mem), .in3(A_mem), .out(A_bus), .sel(in_9));
  Multiplexer #(.select(2), .width(6), .enable("false")) multiplexer_3 (
    .in0({6{1'b0}}), .in1(B_alu), .in2(B_mem), .in3(B_mem), .out(B_bus), .sel(in_9));
  Multiplexer #(.select(2), .width(6), .enable("false")) multiplexer_4 (
    .in0({6{1'b0}}), .in1(C_alu), .in2(C_mem), .in3(C_mem), .out(C_bus), .sel(in_9));

  // Other names for the same wires on the sheet: mux_select[1:0] = in_9
endmodule
