// Logisim project jumpCond_.circ as structural Verilog: 1 circuit, main circuit jumpCont
module jumpCont (
  input  [5:0] T_antes,
  input  [5:0] T_despues,
  input  lo_tomo,
  output mux_selector,
  output hay_jump_en_1,
  output preoload_enable
);

  wire and_1_out, comparator_1_eq, comparator_2_eq, comparator_3_eq, comparator_4_eq, comparator_5_eq,
       comparator_6_eq, comparator_7_eq, comparator_8_eq, comparator_9_eq, or_1_out, or_2_out, or_4_out;

  Comparator #(.width(6)) comparator_1 (.a(T_antes), .b(6'b100000), .eq(comparator_1_eq));  // open: gt, lt
  Comparator #(.width(6)) comparator_2 (.a(T_antes), .b(6'b100011), .eq(comparator_2_eq));  // open: gt, lt
  Comparator #(.width(6)) comparator_3 (.a(T_antes), .b(6'b100100), .eq(comparator_3_eq));  // open: gt, lt
  Comparator #(.width(6)) comparator_4 (.a(T_antes), .b(6'b101000), .eq(comparator_4_eq));  // open: gt, lt
  Comparator #(.width(6)) comparator_5 (.a(T_antes), .b(6'b100001), .eq(comparator_5_eq));  // open: gt, lt
  Comparator #(.width(6)) comparator_6 (.a(T_antes), .b(6'b100010), .eq(comparator_6_eq));  // open: gt, lt
  Comparator #(.width(6)) comparator_7 (.a(T_despues), .b(6'b101000), .eq(comparator_7_eq));  // open: gt, lt
  Comparator #(.width(6)) comparator_8 (.a(T_despues), .b(6'b100001), .eq(comparator_8_eq));  // open: gt, lt
  Comparator #(.width(6)) comparator_9 (.a(T_despues), .b(6'b100010), .eq(comparator_9_eq));  // open: gt, lt
  or or_1 (or_1_out, comparator_1_eq, comparator_2_eq, comparator_3_eq);
  or or_2 (or_2_out, comparator_4_eq, comparator_5_eq, comparator_6_eq);
  or or_3 (hay_jump_en_1, comparator_7_eq, comparator_8_eq, comparator_9_eq);
  and and_1 (and_1_out, hay_jump_en_1, lo_tomo);
  or or_4 (or_4_out, or_2_out, hay_jump_en_1);
  or or_5 (preoload_enable, and_1_out, or_1_out);
  and and_2 (mux_selector, or_4_out, lo_tomo);
endmodule
