// Logisim project register_bank.circ as structural Verilog: 1 circuit, main circuit register_bank
module register_bank (
  input  clk,
  input  [15:0] register_in_data,
  input  [5:0] register_in_address,
  input  [5:0] register_out_A_address,
  input  [5:0] register_out_B_address,
  input  [4:0] register_out_aux_address,
  output [15:0] register_out_A_data,
  output [15:0] register_out_B_data,
  output [15:0] register_out_aux_data
);

  wire not_1_out, reset;
  wire [3:0] decoder_1_out0, decoder_1_out4, decoder_1_out8, decoder_1_out12, decoder_1_out16,
       decoder_1_out20, decoder_1_out24, decoder_1_out28;
  wire [15:0] register_1_q, register_2_q, register_3_q, register_4_q, register_5_q, register_6_q,
       register_7_q, register_8_q, register_9_q, register_10_q, register_11_q, register_12_q, register_13_q,
       register_14_q, register_15_q, register_16_q, register_17_q, register_18_q, register_19_q,
       register_20_q, register_21_q, register_22_q, register_23_q, register_24_q, register_25_q,
       register_26_q, register_27_q, register_28_q, register_29_q, register_30_q, register_31_q,
       register_32_q;

  not not_1 (not_1_out, register_in_address[5]);
  Decoder #(.select(5)) decoder_1 (
    .out0(decoder_1_out0[0]), .out1(decoder_1_out0[1]), .out2(decoder_1_out0[2]), .out3(decoder_1_out0[3]),
    .out4(decoder_1_out4[0]), .out5(decoder_1_out4[1]), .out6(decoder_1_out4[2]), .out7(decoder_1_out4[3]),
    .out8(decoder_1_out8[0]), .out9(decoder_1_out8[1]), .out10(decoder_1_out8[2]), .out11(decoder_1_out8[3]),
    .out12(decoder_1_out12[0]), .out13(decoder_1_out12[1]), .out14(decoder_1_out12[2]),
    .out15(decoder_1_out12[3]), .out16(decoder_1_out16[0]), .out17(decoder_1_out16[1]),
    .out18(decoder_1_out16[2]), .out19(decoder_1_out16[3]), .out20(decoder_1_out20[0]),
    .out21(decoder_1_out20[1]), .out22(decoder_1_out20[2]), .out23(decoder_1_out20[3]),
    .out24(decoder_1_out24[0]), .out25(decoder_1_out24[1]), .out26(decoder_1_out24[2]),
    .out27(decoder_1_out24[3]), .out28(decoder_1_out28[0]), .out29(decoder_1_out28[1]),
    .out30(decoder_1_out28[2]), .out31(decoder_1_out28[3]), .sel(register_in_address[4:0]), .en(not_1_out));
  Register #(.width(16)) register_1 (
    .D(register_in_data), .en(decoder_1_out0[0]), .clk(clk), .Q(register_1_q), .clr(reset));
  Register #(.width(16)) register_2 (
    .D(register_in_data), .en(decoder_1_out4[0]), .clk(clk), .Q(register_2_q), .clr(reset));
  Register #(.width(16)) register_3 (
    .D(register_in_data), .en(decoder_1_out8[0]), .clk(clk), .Q(register_3_q), .clr(reset));
  Register #(.width(16)) register_4 (
    .D(register_in_data), .en(decoder_1_out12[0]), .clk(clk), .Q(register_4_q), .clr(reset));
  Register #(.width(16)) register_5 (
    .D(register_in_data), .en(decoder_1_out16[0]), .clk(clk), .Q(register_5_q), .clr(reset));
  Register #(.width(16)) register_6 (
    .D(register_in_data), .en(decoder_1_out20[0]), .clk(clk), .Q(register_6_q), .clr(reset));
  Register #(.width(16)) register_7 (
    .D(register_in_data), .en(decoder_1_out24[0]), .clk(clk), .Q(register_7_q), .clr(reset));
  Register #(.width(16)) register_8 (
    .D(register_in_data), .en(decoder_1_out28[0]), .clk(clk), .Q(register_8_q), .clr(reset));
  Register #(.width(16)) register_9 (
    .D(register_in_data), .en(decoder_1_out0[1]), .clk(clk), .Q(register_9_q), .clr(reset));
  Register #(.width(16)) register_10 (
    .D(register_in_data), .en(decoder_1_out4[1]), .clk(clk), .Q(register_10_q), .clr(reset));
  Register #(.width(16)) register_11 (
    .D(register_in_data), .en(decoder_1_out8[1]), .clk(clk), .Q(register_11_q), .clr(reset));
  Register #(.width(16)) register_12 (
    .D(register_in_data), .en(decoder_1_out12[1]), .clk(clk), .Q(register_12_q), .clr(reset));
  Register #(.width(16)) register_13 (
    .D(register_in_data), .en(decoder_1_out16[1]), .clk(clk), .Q(register_13_q), .clr(reset));
  Register #(.width(16)) register_14 (
    .D(register_in_data), .en(decoder_1_out20[1]), .clk(clk), .Q(register_14_q), .clr(reset));
  Register #(.width(16)) register_15 (
    .D(register_in_data), .en(decoder_1_out24[1]), .clk(clk), .Q(register_15_q), .clr(reset));
  Register #(.width(16)) register_16 (
    .D(register_in_data), .en(decoder_1_out28[1]), .clk(clk), .Q(register_16_q), .clr(reset));
  Register #(.width(16)) register_17 (
    .D(register_in_data), .en(decoder_1_out0[2]), .clk(clk), .Q(register_17_q), .clr(reset));
  Register #(.width(16)) register_18 (
    .D(register_in_data), .en(decoder_1_out4[2]), .clk(clk), .Q(register_18_q), .clr(reset));
  Register #(.width(16)) register_19 (
    .D(register_in_data), .en(decoder_1_out8[2]), .clk(clk), .Q(register_19_q), .clr(reset));
  Register #(.width(16)) register_20 (
    .D(register_in_data), .en(decoder_1_out12[2]), .clk(clk), .Q(register_20_q), .clr(reset));
  Register #(.width(16)) register_21 (
    .D(register_in_data), .en(decoder_1_out16[2]), .clk(clk), .Q(register_21_q), .clr(reset));
  Register #(.width(16)) register_22 (
    .D(register_in_data), .en(decoder_1_out20[2]), .clk(clk), .Q(register_22_q), .clr(reset));
  Register #(.width(16)) register_23 (
    .D(register_in_data), .en(decoder_1_out24[2]), .clk(clk), .Q(register_23_q), .clr(reset));
  Register #(.width(16)) register_24 (
    .D(register_in_data), .en(decoder_1_out28[2]), .clk(clk), .Q(register_24_q), .clr(reset));
  Register #(.width(16)) register_25 (
    .D(register_in_data), .en(decoder_1_out0[3]), .clk(clk), .Q(register_25_q), .clr(reset));
  Register #(.width(16)) register_26 (
    .D(register_in_data), .en(decoder_1_out4[3]), .clk(clk), .Q(register_26_q), .clr(reset));
  Register #(.width(16)) register_27 (
    .D(register_in_data), .en(decoder_1_out8[3]), .clk(clk), .Q(register_27_q), .clr(reset));
  Register #(.width(16)) register_28 (
    .D(register_in_data), .en(decoder_1_out12[3]), .clk(clk), .Q(register_28_q), .clr(reset));
  Register #(.width(16)) register_29 (
    .D(register_in_data), .en(decoder_1_out16[3]), .clk(clk), .Q(register_29_q), .clr(reset));
  Register #(.width(16)) register_30 (
    .D(register_in_data), .en(decoder_1_out20[3]), .clk(clk), .Q(register_30_q), .clr(reset));
  Register #(.width(16)) register_31 (
    .D(register_in_data), .en(decoder_1_out24[3]), .clk(clk), .Q(register_31_q), .clr(reset));
  Register #(.width(16)) register_32 (
    .D(register_in_data), .en(decoder_1_out28[3]), .clk(clk), .Q(register_32_q), .clr(reset));
  Multiplexer #(.select(5), .width(16), .enable("false")) multiplexer_1 (
    .in0(register_1_q), .in1(register_9_q), .in2(register_17_q), .in3(register_25_q), .in4(register_2_q),
    .in5(register_10_q), .in6(register_18_q), .in7(register_26_q), .in8(register_3_q), .in9(register_11_q),
    .in10(register_19_q), .in11(register_27_q), .in12(register_4_q), .in13(register_12_q),
    .in14(register_20_q), .in15(register_28_q), .in16(register_5_q), .in17(register_13_q),
    .in18(register_21_q), .in19(register_29_q), .in20(register_6_q), .in21(register_14_q),
    .in22(register_22_q), .in23(register_30_q), .in24(register_7_q), .in25(register_15_q),
    .in26(register_23_q), .in27(register_31_q), .in28(register_8_q), .in29(register_16_q),
    .in30(register_24_q), .in31(register_32_q), .out(register_out_A_data), .sel(register_out_A_address[4:0]));
  Multiplexer #(.select(5), .width(16), .enable("false")) multiplexer_2 (
    .in0(register_1_q), .in1(register_9_q), .in2(register_17_q), .in3(register_25_q), .in4(register_2_q),
    .in5(register_10_q), .in6(register_18_q), .in7(register_26_q), .in8(register_3_q), .in9(register_11_q),
    .in10(register_19_q), .in11(register_27_q), .in12(register_4_q), .in13(register_12_q),
    .in14(register_20_q), .in15(register_28_q), .in16(register_5_q), .in17(register_13_q),
    .in18(register_21_q), .in19(register_29_q), .in20(register_6_q), .in21(register_14_q),
    .in22(register_22_q), .in23(register_30_q), .in24(register_7_q), .in25(register_15_q),
    .in26(register_23_q), .in27(register_31_q), .in28(register_8_q), .in29(register_16_q),
    .in30(register_24_q), .in31(register_32_q), .out(register_out_B_data), .sel(register_out_B_address[4:0]));
  Multiplexer #(.select(5), .width(16), .enable("false")) multiplexer_3 (
    .in0(register_1_q), .in1(register_9_q), .in2(register_17_q), .in3(register_25_q), .in4(register_2_q),
    .in5(register_10_q), .in6(register_18_q), .in7(register_26_q), .in8(register_3_q), .in9(register_11_q),
    .in10(register_19_q), .in11(register_27_q), .in12(register_4_q), .in13(register_12_q),
    .in14(register_20_q), .in15(register_28_q), .in16(register_5_q), .in17(register_13_q),
    .in18(register_21_q), .in19(register_29_q), .in20(register_6_q), .in21(register_14_q),
    .in22(register_22_q), .in23(register_30_q), .in24(register_7_q), .in25(register_15_q),
    .in26(register_23_q), .in27(register_31_q), .in28(register_8_q), .in29(register_16_q),
    .in30(register_24_q), .in31(register_32_q), .out(register_out_aux_data), .sel(register_out_aux_address));
  // OR_Gate or_1 is placed but not wired
endmodule
