// Logisim project return_address_stack_.circ as structural Verilog: 1 circuit, main circuit return_address_stack
module return_address_stack (
  input  PUSH,
  input  POP,
  input  CLK,
  input  [10:0] PC,
  output [10:0] TOS
);

  wire and_1_out, and_2_out, and_3_out, and_4_out, and_5_out, j_k_ff_1_qn, not_1_out, not_2_out, or_1_out,
       or_2_out;
  wire [1:0] j_k_ff_1_q;
  wire [10:0] adder_1_out, register_1_q;

  or or_1 (or_1_out, POP, PUSH);
  not not_1 (not_1_out, PUSH);
  not not_2 (not_2_out, not_1_out);
  J_K_Flip_Flop #(.trigger("falling")) j_k_ff_1 (
    .J(or_1_out), .K(or_1_out), .clk(CLK), .Q(j_k_ff_1_q[0]), .Qn(j_k_ff_1_qn));  // open: preset, reset
  Adder #(.width(11)) adder_1 (.a(11'h1), .b(PC), .out(adder_1_out), .cin(1'b0));  // open: cout
  and and_1 (and_1_out, not_1_out, not_2_out);
  and and_2 (and_2_out, PUSH, j_k_ff_1_q[0]);
  or or_2 (or_2_out, and_2_out, and_3_out);
  and and_3 (and_3_out, j_k_ff_1_qn, ~PUSH);  // AND_Gate
  Register #(.width(11)) register_1 (.D(adder_1_out), .en(1'b1), .clk(PUSH), .Q(register_1_q));  // open: clr
  J_K_Flip_Flop #(.trigger("falling")) j_k_ff_2 (
    .J(and_4_out), .K(and_5_out), .clk(CLK), .Q(j_k_ff_1_q[1]));  // open: Qn, preset, reset
  and and_4 (and_4_out, or_1_out, or_2_out);
  and and_5 (and_5_out, or_2_out, or_1_out);
  RAM #(.addrWidth(2), .dataWidth(11), .trigger("high"), .databus("bibus")) ram_1 (
    .addr(j_k_ff_1_q), .we(and_1_out), .oe(POP), .din(register_1_q), .dout(TOS));

  // Notes on the sheet:
  //   enable
  //   b0
  //   b1
endmodule
