// Logisim project shiftershsh.circ as structural Verilog: 1 circuit, main circuit ShifterSH
module ShifterSH (
  input  [15:0] ShifterIn,
  input  [1:0] SH,
  output [15:0] out_3
);

  wire [15:0] shifter_1_out, shifter_2_out;

  Shifter #(.width(16), .shift("lr")) shifter_1 (.in(ShifterIn), .\dist (4'b0001), .out(shifter_1_out));
  Shifter #(.width(16)) shifter_2 (.in(ShifterIn), .\dist (4'b0001), .out(shifter_2_out));
  Multiplexer #(.select(2), .width(16), .enable("false")) multiplexer_1 (
    .in0(ShifterIn), .in1(shifter_1_out), .in2(shifter_2_out), .in3(ShifterIn), .out(out_3), .sel(SH));
endmodule
