// Logisim project viewers.circ as structural Verilog: 9 circuits, main circuit pipeline_register_viewer
module pipeline_register_viewer (
  input  [14:0] microinstruction,
  input  [5:0] A_in,
  input  [5:0] B_in,
  input  [5:0] C_in,
  output [3:0] b16,
  output [3:0] b15,
  output [3:0] b14,
  output [3:0] b13,
  output [3:0] b12,
  output [3:0] b11,
  output [3:0] b10,
  output [3:0] b9,
  output [3:0] b8,
  output [3:0] b7,
  output [3:0] b6,
  output [3:0] b5,
  output [3:0] b4,
  output [3:0] b3,
  output [3:0] b2,
  output [3:0] b1,
  output [3:0] b0,
  output A_is_enabled,
  output [3:0] A_MSN,
  output [3:0] A_LSN,
  output B_is_enabled,
  output [3:0] B_MSN,
  output [3:0] B_LSN,
  output C_is_enabled,
  output [3:0] C_MSN,
  output [3:0] C_LSN
);

  wire comparator_1_eq, comparator_2_eq, comparator_3_eq, comparator_4_eq, comparator_5_eq, comparator_6_eq,
       comparator_7_eq, comparator_8_eq, comparator_9_eq, comparator_10_eq, comparator_11_eq,
       comparator_12_eq, comparator_13_eq, comparator_14_eq, comparator_15_eq, comparator_16_eq,
       comparator_17_eq, comparator_18_eq, comparator_19_eq, comparator_20_eq, comparator_21_eq,
       comparator_22_eq, comparator_23_eq;

  Comparator #(.width(15)) comparator_1 (.a(15'h102), .b(microinstruction), .eq(comparator_1_eq));  // open: gt, lt
  Comparator #(.width(15)) comparator_2 (.a(15'h3903), .b(microinstruction), .eq(comparator_2_eq));  // open: gt, lt
  Comparator #(.width(15)) comparator_3 (.a(15'h3103), .b(microinstruction), .eq(comparator_3_eq));  // open: gt, lt
  Comparator #(.width(15)) comparator_4 (.a(15'h291b), .b(microinstruction), .eq(comparator_4_eq));  // open: gt, lt
  Comparator #(.width(15)) comparator_5 (.a(15'h20), .b(microinstruction), .eq(comparator_5_eq));  // open: gt, lt
  Comparator #(.width(15)) comparator_6 (.a(15'h28), .b(microinstruction), .eq(comparator_6_eq));  // open: gt, lt
  Comparator #(.width(15)) comparator_7 (.a(15'h21), .b(microinstruction), .eq(comparator_7_eq));  // open: gt, lt
  Comparator #(.width(15)) comparator_8 (.a(15'h22), .b(microinstruction), .eq(comparator_8_eq));  // open: gt, lt
  Comparator #(.width(15)) comparator_9 (.a(15'h82), .b(microinstruction), .eq(comparator_9_eq));  // open: gt, lt
  Comparator #(.width(15)) comparator_10 (.a(15'h41), .b(microinstruction), .eq(comparator_10_eq));  // open: gt, lt
  Comparator #(.width(15)) comparator_11 (.a(15'h23), .b(microinstruction), .eq(comparator_11_eq));  // open: gt, lt
  Comparator #(.width(15)) comparator_12 (.a(15'h281f), .b(microinstruction), .eq(comparator_12_eq));  // open: gt, lt
  Comparator #(.width(15)) comparator_13 (.a(15'h3), .b(microinstruction), .eq(comparator_13_eq));  // open: gt, lt
  Comparator #(.width(15)) comparator_14 (.a(15'h3007), .b(microinstruction), .eq(comparator_14_eq));  // open: gt, lt
  Comparator #(.width(15)) comparator_15 (.a(15'h3807), .b(microinstruction), .eq(comparator_15_eq));  // open: gt, lt
  Comparator #(.width(15)) comparator_16 (.a(15'h1803), .b(microinstruction), .eq(comparator_16_eq));  // open: gt, lt
  Comparator #(.width(15)) comparator_17 (.a(15'h203), .b(microinstruction), .eq(comparator_17_eq));  // open: gt, lt
  Comparator #(.width(15)) comparator_18 (.a(15'h403), .b(microinstruction), .eq(comparator_18_eq));  // open: gt, lt
  Comparator #(.width(15)) comparator_19 (.a(15'h603), .b(microinstruction), .eq(comparator_19_eq));  // open: gt, lt
  Comparator #(.width(15)) comparator_20 (.a(15'h5810), .b(microinstruction), .eq(comparator_20_eq));  // open: gt, lt
  Comparator #(.width(15)) comparator_21 (.a(15'h6010), .b(microinstruction), .eq(comparator_21_eq));  // open: gt, lt
  Comparator #(.width(15)) comparator_22 (.a(15'h24), .b(microinstruction), .eq(comparator_22_eq));  // open: gt, lt
  Comparator #(.width(15)) comparator_23 (.a({15{1'b0}}), .b(microinstruction), .eq(comparator_23_eq));  // open: gt, lt
  assign {b4, b3, b2, b1, b0} = comparator_1_eq ? 20'hf44a9 : 20'bz;  // Controlled_Buffer controlled_buffer_1
  assign {b10, b9, b8, b7, b6} = comparator_1_eq ? 20'h69996 : 20'bz;  // Controlled_Buffer controlled_buffer_2
  assign {b4, b3, b2, b1, b0} = comparator_2_eq ? 20'hf44a9 : 20'bz;  // Controlled_Buffer controlled_buffer_3
  assign {b10, b9, b8, b7, b6} = comparator_2_eq ? 20'hf842f : 20'bz;  // Controlled_Buffer controlled_buffer_4
  assign {b10, b9, b8, b7, b6} = comparator_3_eq ? 20'hfaaa5 : 20'bz;  // Controlled_Buffer controlled_buffer_5
  assign {b4, b3, b2, b1, b0} = comparator_3_eq ? 20'hf44a9 : 20'bz;  // Controlled_Buffer controlled_buffer_6
  assign {b4, b3, b2, b1, b0} = comparator_4_eq ? 20'hf44a9 : 20'bz;  // Controlled_Buffer controlled_buffer_7
  assign {b10, b9, b8, b7, b6} = comparator_4_eq ? 20'hf9996 : 20'bz;  // Controlled_Buffer controlled_buffer_8
  assign {b4, b3, b2, b1, b0} = comparator_5_eq ? 20'hfaaa4 : 20'bz;  // Controlled_Buffer controlled_buffer_9
  assign {b10, b9, b8, b7, b6} = comparator_5_eq ? 20'hf424f : 20'bz;  // Controlled_Buffer controlled_buffer_10
  assign {b10, b9, b8, b7, b6} = comparator_6_eq ? 20'h69999 : 20'bz;  // Controlled_Buffer controlled_buffer_11
  assign {b4, b3, b2, b1, b0} = comparator_6_eq ? 20'h69999 : 20'bz;  // Controlled_Buffer controlled_buffer_12
  assign {b10, b9, b8, b7, b6} = comparator_7_eq ? 20'hf842f : 20'bz;  // Controlled_Buffer controlled_buffer_13
  assign {b4, b3, b2, b1, b0} = comparator_7_eq ? 20'h69bd1 : 20'bz;  // Controlled_Buffer controlled_buffer_14
  assign {b4, b3, b2, b1, b0} = comparator_8_eq ? 20'h69bd1 : 20'bz;  // Controlled_Buffer controlled_buffer_15
  assign {b10, b9, b8, b7, b6} = comparator_8_eq ? 20'h9bd9 : 20'bz;  // Controlled_Buffer controlled_buffer_16
  assign {b10, b9, b8, b7, b6} = comparator_9_eq ? 20'h69996 : 20'bz;  // Controlled_Buffer controlled_buffer_17
  assign {b4, b3, b2, b1, b0} = comparator_9_eq ? 20'hf424f : 20'bz;  // Controlled_Buffer controlled_buffer_18
  assign {b4, b3, b2, b1, b0} = comparator_10_eq ? 20'hf424f : 20'bz;  // Controlled_Buffer controlled_buffer_19
  assign {b10, b9, b8, b7, b6} = comparator_10_eq ? 20'h69996 : 20'bz;  // Controlled_Buffer controlled_buffer_20
  assign {b4, b3, b2, b1, b0} = comparator_11_eq ? 20'hfaaa5 : 20'bz;  // Controlled_Buffer controlled_buffer_21
  assign {b10, b9, b8, b7, b6} = comparator_11_eq ? 20'h1db8 : 20'bz;  // Controlled_Buffer controlled_buffer_22
  assign {b10, b9, b8, b7, b6} = comparator_12_eq ? 20'hf9996 : 20'bz;  // Controlled_Buffer controlled_buffer_23
  assign {b4, b3, b2, b1, b0} = comparator_12_eq ? 20'hfaaa5 : 20'bz;  // Controlled_Buffer controlled_buffer_24
  assign {b4, b3, b2, b1, b0} = comparator_13_eq ? 20'hc212c : 20'bz;  // Controlled_Buffer controlled_buffer_25
  assign {b10, b9, b8, b7, b6} = comparator_13_eq ? 20'h69996 : 20'bz;  // Controlled_Buffer controlled_buffer_26
  assign {b10, b9, b8, b7, b6} = comparator_14_eq ? 20'hfaaa5 : 20'bz;  // Controlled_Buffer controlled_buffer_27
  assign {b4, b3, b2, b1, b0} = comparator_14_eq ? 20'hfaaa5 : 20'bz;  // Controlled_Buffer controlled_buffer_28
  assign {b10, b9, b8, b7, b6} = comparator_15_eq ? 20'hf842f : 20'bz;  // Controlled_Buffer controlled_buffer_29
  assign {b4, b3, b2, b1, b0} = comparator_15_eq ? 20'hfaaa5 : 20'bz;  // Controlled_Buffer controlled_buffer_30
  assign {b4, b3, b2, b1, b0} = comparator_16_eq ? 20'hf1111 : 20'bz;  // Controlled_Buffer controlled_buffer_31
  assign {b10, b9, b8, b7, b6} = comparator_16_eq ? 20'hfaaa4 : 20'bz;  // Controlled_Buffer controlled_buffer_32
  assign {b10, b9, b8, b7, b6} = comparator_17_eq ? 20'h1db8 : 20'bz;  // Controlled_Buffer controlled_buffer_33
  assign {b4, b3, b2, b1, b0} = comparator_17_eq ? 20'hfaaa5 : 20'bz;  // Controlled_Buffer controlled_buffer_34
  assign {b4, b3, b2, b1, b0} = comparator_18_eq ? 20'hf1111 : 20'bz;  // Controlled_Buffer controlled_buffer_35
  assign {b10, b9, b8, b7, b6} = comparator_18_eq ? 20'h1db8 : 20'bz;  // Controlled_Buffer controlled_buffer_36
  assign {b4, b3, b2, b1, b0} = comparator_19_eq ? 20'hfaaa5 : 20'bz;  // Controlled_Buffer controlled_buffer_37
  assign {b10, b9, b8, b7, b6} = comparator_19_eq ? 20'h1db8 : 20'bz;  // Controlled_Buffer controlled_buffer_38
  assign {b4, b3, b2, b1, b0} = comparator_20_eq ? 20'hfaaa5 : 20'bz;  // Controlled_Buffer controlled_buffer_39
  assign {b10, b9, b8, b7, b6} = comparator_20_eq ? 20'hf1111 : 20'bz;  // Controlled_Buffer controlled_buffer_40
  assign {b4, b3, b2, b1, b0} = comparator_21_eq ? 20'h88f88 : 20'bz;  // Controlled_Buffer controlled_buffer_41
  assign {b10, b9, b8, b7, b6} = comparator_21_eq ? 20'h69bd1 : 20'bz;  // Controlled_Buffer controlled_buffer_42
  assign {b10, b9, b8, b7, b6} = comparator_22_eq ? 20'h69bd1 : 20'bz;  // Controlled_Buffer controlled_buffer_43
  assign {b4, b3, b2, b1, b0} = comparator_22_eq ? 20'h88f88 : 20'bz;  // Controlled_Buffer controlled_buffer_44
  assign {b4, b3, b2, b1, b0} = comparator_23_eq ? {20{1'b1}} : 20'bz;  // Controlled_Buffer controlled_buffer_45
  assign {b10, b9, b8, b7, b6} = comparator_23_eq ? {20{1'b1}} : 20'bz;  // Controlled_Buffer controlled_buffer_46
  assign {b16, b15, b14, b13, b12} = comparator_1_eq ? 20'hf424f : 20'bz;  // Controlled_Buffer controlled_buffer_47
  assign {b16, b15, b14, b13, b12} = comparator_2_eq ? 20'h36a63 : 20'bz;  // Controlled_Buffer controlled_buffer_48
  assign {b16, b15, b14, b13, b12} = comparator_3_eq ? 20'h69996 : 20'bz;  // Controlled_Buffer controlled_buffer_49
  assign {b16, b15, b14, b13, b12} = comparator_4_eq ? 20'h36a63 : 20'bz;  // Controlled_Buffer controlled_buffer_50
  assign {b16, b15, b14, b13, b12} = comparator_5_eq ? 20'h2999e : 20'bz;  // Controlled_Buffer controlled_buffer_51
  assign {b16, b15, b14, b13, b12} = comparator_6_eq ? 20'h2999e : 20'bz;  // Controlled_Buffer controlled_buffer_52
  assign {b16, b15, b14, b13, b12} = comparator_7_eq ? 20'h2999e : 20'bz;  // Controlled_Buffer controlled_buffer_53
  assign {b16, b15, b14, b13, b12} = comparator_8_eq ? 20'h2999e : 20'bz;  // Controlled_Buffer controlled_buffer_54
  assign {b16, b15, b14, b13, b12} = comparator_9_eq ? 20'hf424f : 20'bz;  // Controlled_Buffer controlled_buffer_55
  assign {b16, b15, b14, b13, b12} = comparator_10_eq ? 20'hf424f : 20'bz;  // Controlled_Buffer controlled_buffer_56
  assign {b16, b15, b14, b13, b12} = comparator_11_eq ? 20'hf5552 : 20'bz;  // Controlled_Buffer controlled_buffer_57
  assign {b16, b15, b14, b13, b12} = comparator_12_eq ? 20'h36a63 : 20'bz;  // Controlled_Buffer controlled_buffer_58
  assign {b16, b15, b14, b13, b12} = comparator_13_eq ? 20'hf424f : 20'bz;  // Controlled_Buffer controlled_buffer_59
  assign {b16, b15, b14, b13, b12} = comparator_14_eq ? 20'h69996 : 20'bz;  // Controlled_Buffer controlled_buffer_60
  assign {b16, b15, b14, b13, b12} = comparator_15_eq ? 20'h36a63 : 20'bz;  // Controlled_Buffer controlled_buffer_61
  assign {b16, b15, b14, b13, b12} = comparator_16_eq ? 20'h69999 : 20'bz;  // Controlled_Buffer controlled_buffer_62
  assign {b16, b15, b14, b13, b12} = comparator_17_eq ? 20'h36a63 : 20'bz;  // Controlled_Buffer controlled_buffer_63
  assign {b16, b15, b14, b13, b12} = comparator_18_eq ? 20'hf1111 : 20'bz;  // Controlled_Buffer controlled_buffer_64
  assign {b16, b15, b14, b13, b12} = comparator_19_eq ? 20'hf1111 : 20'bz;  // Controlled_Buffer controlled_buffer_65
  assign {b16, b15, b14, b13, b12} = comparator_20_eq ? 20'h69999 : 20'bz;  // Controlled_Buffer controlled_buffer_66
  assign {b16, b15, b14, b13, b12} = comparator_21_eq ? 20'h1db8 : 20'bz;  // Controlled_Buffer controlled_buffer_67
  assign {b16, b15, b14, b13, b12} = comparator_22_eq ? 20'hfaaa5 : 20'bz;  // Controlled_Buffer controlled_buffer_68
  assign {b16, b15, b14, b13, b12} = comparator_23_eq ? {20{1'b1}} : 20'bz;  // Controlled_Buffer controlled_buffer_69
  not not_1 (A_MSN[3], A_in[5]);
  not not_2 (B_MSN[3], B_in[5]);
  not not_3 (C_MSN[3], C_in[5]);

  assign A_is_enabled = A_in[5];
  assign A_LSN = A_in[3:0];
  assign A_MSN[2:0] = {{2{A_MSN[3]}}, A_in[4]};
  assign b5 = 4'b0000;
  assign b11 = 4'b0000;
  assign B_is_enabled = B_in[5];
  assign B_LSN = B_in[3:0];
  assign B_MSN[2:0] = {{2{B_MSN[3]}}, B_in[4]};
  assign C_is_enabled = C_in[5];
  assign C_LSN = C_in[3:0];
  assign C_MSN[2:0] = {{2{C_MSN[3]}}, C_in[4]};

  // Notes on the sheet:
  //   A
  //   B
  //   C
  //   D
  //   E
  //   J
  //   K
  //   L
  //   M
  //   N
  //   O
  //   P
  //   R
  //   S
  //   T
  //   V
  //   Y
  //   Z
  //   MOK
  //   ANK
  //   ORK
  //   ADK
  //   JMP
  //   JCY
  //   JNE
  //   JZE
  //   MOM
  //   MOM
  //   BSR
  //   ADR
  //   MOV
  //   ORR
  //   ANR
  //   CPL
  //   ASR
  //   LSL
  //   LSR
  //   CLR
  //   SET
  //   RET
  //   M
  //   O
  //   K
  //   A
  //   N
  //   K
  //   O
  //   R
  //   K
  //   A
  //   D
  //   K
  //   J
  //   M
  //   P
  //   J
  //   C
  //   Y
  //   J
  //   N
  //   E
  //   J
  //   Z
  //   E
  //   M
  //   O
  //   M
  //   M
  //   O
  //   M
  //   B
  //   S
  //   R
  //   A
  //   D
  //   R
  //   M
  //   O
  //   V
  //   O
  //   R
  //   R
  //   A
  //   N
  //   R
  //   C
  //   P
  //   L
  //   A
  //   S
  //   R
  //   L
  //   S
  //   L
  //   L
  //   S
  //   R
  //   C
  //   L
  //   R
  //   S
  //   E
  //   T
  //   R
  //   E
  //   T
endmodule

module register_bank_viewer (
  input  [5:0] A_data_out,
  input  [15:0] A_address,
  input  [5:0] B_data_out,
  input  [15:0] B_address,
  input  [5:0] C_data_out,
  input  [15:0] C_address,
  output A_is_enabled,
  output [3:0] A_data_MSN,
  output [3:0] A_data_LSN,
  output [3:0] A_address_N3,
  output [3:0] A_address_N2,
  output [3:0] A_address_N1,
  output [3:0] A_address_N0,
  output B_is_enabled,
  output [3:0] B_data_MSN,
  output [3:0] B_data_LSN,
  output [3:0] B_address_N3,
  output [3:0] B_address_N2,
  output [3:0] B_address_N1,
  output [3:0] B_address_N0,
  output C_is_enabled,
  output [3:0] C_data_MSN,
  output [3:0] C_data_LSN,
  output [3:0] C_address_N3,
  output [3:0] C_address_N2,
  output [3:0] C_address_N1,
  output [3:0] C_address_N0
);

  not not_1 (A_data_MSN[3], A_data_out[5]);
  not not_2 (B_data_MSN[3], B_data_out[5]);
  not not_3 (C_data_MSN[3], C_data_out[5]);

  assign A_address_N0 = A_address[3:0];
  assign A_address_N1 = A_address[7:4];
  assign A_address_N2 = A_address[11:8];
  assign A_address_N3 = A_address[15:12];
  assign A_data_LSN = A_data_out[3:0];
  assign A_data_MSN[2:0] = {{2{A_data_MSN[3]}}, A_data_out[4]};
  assign A_is_enabled = A_data_out[5];
  assign B_address_N0 = B_address[3:0];
  assign B_address_N1 = B_address[7:4];
  assign B_address_N2 = B_address[11:8];
  assign B_address_N3 = B_address[15:12];
  assign B_data_LSN = B_data_out[3:0];
  assign B_data_MSN[2:0] = {{2{B_data_MSN[3]}}, B_data_out[4]};
  assign B_is_enabled = B_data_out[5];
  assign C_address_N0 = C_address[3:0];
  assign C_address_N1 = C_address[7:4];
  assign C_address_N2 = C_address[11:8];
  assign C_address_N3 = C_address[15:12];
  assign C_data_LSN = C_data_out[3:0];
  assign C_data_MSN[2:0] = {{2{C_data_MSN[3]}}, C_data_out[4]};
  assign C_is_enabled = C_data_out[5];
endmodule

module UC2_viewer (
  input  hold,
  output [7:0] out_2,
  output [7:0] out_3,
  output [7:0] out_4,
  output [7:0] out_5,
  output [7:0] out_6,
  output [7:0] out_7,
  output [7:0] out_8,
  output [7:0] out_9
);

  Multiplexer #(.width(8), .enable("false")) multiplexer_1 (.in0({8{1'b0}}), .in1(8'h3c), .out(out_2), .sel(hold));
  Multiplexer #(.width(8), .enable("false")) multiplexer_2 (.in0({8{1'b0}}), .in1(8'h42), .out(out_3), .sel(hold));
  Multiplexer #(.width(8), .enable("false")) multiplexer_3 (.in0({8{1'b0}}), .in1(8'h85), .out(out_4), .sel(hold));
  Multiplexer #(.width(8), .enable("false")) multiplexer_4 (.in0({8{1'b0}}), .in1(8'h89), .out(out_5), .sel(hold));
  Multiplexer #(.width(8), .enable("false")) multiplexer_5 (.in0({8{1'b0}}), .in1(8'h91), .out(out_6), .sel(hold));
  Multiplexer #(.width(8), .enable("false")) multiplexer_6 (.in0({8{1'b0}}), .in1(8'ha1), .out(out_7), .sel(hold));
  Multiplexer #(.width(8), .enable("false")) multiplexer_7 (.in0({8{1'b0}}), .in1(8'h42), .out(out_8), .sel(hold));
  Multiplexer #(.width(8), .enable("false")) multiplexer_8 (.in0({8{1'b0}}), .in1(8'h3c), .out(out_9), .sel(hold));
endmodule

module clk_edge_viewer (
  input  in_1,
  output [7:0] out_2,
  output [7:0] out_3,
  output [7:0] out_4,
  output [7:0] out_5,
  output [7:0] out_6,
  output [7:0] out_7,
  output [7:0] out_8,
  output [7:0] out_9
);

  Multiplexer #(.width(8), .enable("false")) multiplexer_1 (.in0(8'h80), .in1(8'h1), .out(out_2), .sel(in_1));
  Multiplexer #(.width(8), .enable("false")) multiplexer_2 (.in0(8'ha0), .in1(8'h9), .out(out_3), .sel(in_1));
  Multiplexer #(.width(8), .enable("false")) multiplexer_3 (.in0(8'h90), .in1(8'h11), .out(out_4), .sel(in_1));
  Multiplexer #(.width(8), .enable("false")) multiplexer_4 (.in0({8{1'b1}}), .in1({8{1'b1}}), .out(out_5), .sel(in_1));
  Multiplexer #(.width(8), .enable("false")) multiplexer_5 (.in0(8'h11), .in1(8'h90), .out(out_6), .sel(in_1));
  Multiplexer #(.width(8), .enable("false")) multiplexer_6 (.in0(8'h21), .in1(8'h88), .out(out_7), .sel(in_1));
  Multiplexer #(.width(8), .enable("false")) multiplexer_7 (.in0(8'h1), .in1(8'h80), .out(out_8), .sel(in_1));
  Multiplexer #(.width(8), .enable("false")) multiplexer_8 (.in0(8'h1), .in1(8'h80), .out(out_9), .sel(in_1));
endmodule

module output_ports_viewer (
  input  [15:0] PO0,
  input  [15:0] PO1,
  output [3:0] hex_disp_0_3,
  output [3:0] hex_disp_0_2,
  output [3:0] hex_disp_0_1,
  output [3:0] hex_disp_0_0,
  output [31:0] MAT_0_COL_3,
  output [31:0] MAT_0_COL_3_2,
  output [31:0] MAT_0_COL_3_3,
  output [31:0] MAT_0_COL_3_4,
  output [31:0] MAT_0_COL_3_5,
  output [31:0] MAT_0_COL_3_6,
  output [31:0] MAT_0_COL_3_7,
  output [31:0] MAT_0_COL_3_8,
  output [31:0] MAT_0_COL_2,
  output [31:0] MAT_0_COL_2_2,
  output [31:0] MAT_0_COL_2_3,
  output [31:0] MAT_0_COL_2_4,
  output [31:0] MAT_0_COL_2_5,
  output [31:0] MAT_0_COL_2_6,
  output [31:0] MAT_0_COL_2_7,
  output [31:0] MAT_0_COL_2_8,
  output [31:0] MAT_0_COL_1,
  output [31:0] MAT_0_COL_1_2,
  output [31:0] MAT_0_COL_1_3,
  output [31:0] MAT_0_COL_1_4,
  output [31:0] MAT_0_COL_1_5,
  output [31:0] MAT_0_COL_1_6,
  output [31:0] MAT_0_COL_1_7,
  output [31:0] MAT_0_COL_1_8,
  output [31:0] MAT_0_COL_0,
  output [31:0] MAT_0_COL_0_2,
  output [31:0] MAT_0_COL_0_3,
  output [31:0] MAT_0_COL_0_4,
  output [31:0] MAT_0_COL_0_5,
  output [31:0] MAT_0_COL_0_6,
  output [31:0] MAT_0_COL_0_7,
  output [31:0] MAT_0_COL_0_8,
  output [3:0] hex_disp_1_3,
  output [3:0] hex_disp_1_2,
  output [3:0] hex_disp_1_1,
  output [3:0] hex_disp_1_0,
  output [31:0] MAT_1_COL_3,
  output [31:0] MAT_1_COL_3_2,
  output [31:0] MAT_1_COL_3_3,
  output [31:0] MAT_1_COL_3_4,
  output [31:0] MAT_1_COL_3_5,
  output [31:0] MAT_1_COL_3_6,
  output [31:0] MAT_1_COL_3_7,
  output [31:0] MAT_1_COL_3_8,
  output [31:0] MAT_1_COL_2,
  output [31:0] MAT_1_COL_2_2,
  output [31:0] MAT_1_COL_2_3,
  output [31:0] MAT_1_COL_2_4,
  output [31:0] MAT_1_COL_2_5,
  output [31:0] MAT_1_COL_2_6,
  output [31:0] MAT_1_COL_2_7,
  output [31:0] MAT_1_COL_2_8,
  output [31:0] MAT_1_COL_1,
  output [31:0] MAT_1_COL_1_2,
  output [31:0] MAT_1_COL_1_3,
  output [31:0] MAT_1_COL_1_4,
  output [31:0] MAT_1_COL_1_5,
  output [31:0] MAT_1_COL_1_6,
  output [31:0] MAT_1_COL_1_7,
  output [31:0] MAT_1_COL_1_8,
  output [31:0] MAT_1_COL_0,
  output [31:0] MAT_1_COL_0_2,
  output [31:0] MAT_1_COL_0_3,
  output [31:0] MAT_1_COL_0_4,
  output [31:0] MAT_1_COL_0_5,
  output [31:0] MAT_1_COL_0_6,
  output [31:0] MAT_1_COL_0_7,
  output [31:0] MAT_1_COL_0_8
);

  output_port_adapter output_port_adapter_1 (
    .PO(PO0), .hex_disp_3(hex_disp_0_3), .hex_disp_2(hex_disp_0_2), .hex_disp_1(hex_disp_0_1),
    .hex_disp_0(hex_disp_0_0), .COL_3(MAT_0_COL_3), .COL_2(MAT_0_COL_2), .COL_1(MAT_0_COL_1),
    .COL_0_4(MAT_0_COL_0));  // open: COL_3_2, COL_3_3, COL_3_4, COL_2_2, COL_2_3, COL_2_4, COL_1_2, COL_1_3, COL_1_4, COL_0, COL_0_2, COL_0_3
  output_port_adapter output_port_adapter_2 (
    .PO(PO1), .hex_disp_3(hex_disp_1_3), .hex_disp_2(hex_disp_1_2), .hex_disp_1(hex_disp_1_1),
    .hex_disp_0(hex_disp_1_0), .COL_3(MAT_1_COL_3), .COL_2(MAT_1_COL_2), .COL_1(MAT_1_COL_1),
    .COL_0(MAT_1_COL_0));  // open: COL_3_2, COL_3_3, COL_3_4, COL_2_2, COL_2_3, COL_2_4, COL_1_2, COL_1_3, COL_1_4, COL_0_2, COL_0_3, COL_0_4

  assign MAT_0_COL_0_2 = MAT_0_COL_0;
  assign MAT_0_COL_0_3 = MAT_0_COL_0;
  assign MAT_0_COL_0_4 = MAT_0_COL_0;
  assign MAT_0_COL_0_5 = MAT_0_COL_0;
  assign MAT_0_COL_0_6 = MAT_0_COL_0;
  assign MAT_0_COL_0_7 = MAT_0_COL_0;
  assign MAT_0_COL_0_8 = MAT_0_COL_0;
  assign MAT_0_COL_1_2 = MAT_0_COL_1;
  assign MAT_0_COL_1_3 = MAT_0_COL_1;
  assign MAT_0_COL_1_4 = MAT_0_COL_1;
  assign MAT_0_COL_1_5 = MAT_0_COL_1;
  assign MAT_0_COL_1_6 = MAT_0_COL_1;
  assign MAT_0_COL_1_7 = MAT_0_COL_1;
  assign MAT_0_COL_1_8 = MAT_0_COL_1;
  assign MAT_0_COL_2_2 = MAT_0_COL_2;
  assign MAT_0_COL_2_3 = MAT_0_COL_2;
  assign MAT_0_COL_2_4 = MAT_0_COL_2;
  assign MAT_0_COL_2_5 = MAT_0_COL_2;
  assign MAT_0_COL_2_6 = MAT_0_COL_2;
  assign MAT_0_COL_2_7 = MAT_0_COL_2;
  assign MAT_0_COL_2_8 = MAT_0_COL_2;
  assign MAT_0_COL_3_2 = MAT_0_COL_3;
  assign MAT_0_COL_3_3 = MAT_0_COL_3;
  assign MAT_0_COL_3_4 = MAT_0_COL_3;
  assign MAT_0_COL_3_5 = MAT_0_COL_3;
  assign MAT_0_COL_3_6 = MAT_0_COL_3;
  assign MAT_0_COL_3_7 = MAT_0_COL_3;
  assign MAT_0_COL_3_8 = MAT_0_COL_3;
  assign MAT_1_COL_0_2 = MAT_1_COL_0;
  assign MAT_1_COL_0_3 = MAT_1_COL_0;
  assign MAT_1_COL_0_4 = MAT_1_COL_0;
  assign MAT_1_COL_0_5 = MAT_1_COL_0;
  assign MAT_1_COL_0_6 = MAT_1_COL_0;
  assign MAT_1_COL_0_7 = MAT_1_COL_0;
  assign MAT_1_COL_0_8 = MAT_1_COL_0;
  assign MAT_1_COL_1_2 = MAT_1_COL_1;
  assign MAT_1_COL_1_3 = MAT_1_COL_1;
  assign MAT_1_COL_1_4 = MAT_1_COL_1;
  assign MAT_1_COL_1_5 = MAT_1_COL_1;
  assign MAT_1_COL_1_6 = MAT_1_COL_1;
  assign MAT_1_COL_1_7 = MAT_1_COL_1;
  assign MAT_1_COL_1_8 = MAT_1_COL_1;
  assign MAT_1_COL_2_2 = MAT_1_COL_2;
  assign MAT_1_COL_2_3 = MAT_1_COL_2;
  assign MAT_1_COL_2_4 = MAT_1_COL_2;
  assign MAT_1_COL_2_5 = MAT_1_COL_2;
  assign MAT_1_COL_2_6 = MAT_1_COL_2;
  assign MAT_1_COL_2_7 = MAT_1_COL_2;
  assign MAT_1_COL_2_8 = MAT_1_COL_2;
  assign MAT_1_COL_3_2 = MAT_1_COL_3;
  assign MAT_1_COL_3_3 = MAT_1_COL_3;
  assign MAT_1_COL_3_4 = MAT_1_COL_3;
  assign MAT_1_COL_3_5 = MAT_1_COL_3;
  assign MAT_1_COL_3_6 = MAT_1_COL_3;
  assign MAT_1_COL_3_7 = MAT_1_COL_3;
  assign MAT_1_COL_3_8 = MAT_1_COL_3;
endmodule

module output_port_adapter (
  input  [15:0] PO,
  output [3:0] hex_disp_3,
  output [3:0] hex_disp_2,
  output [3:0] hex_disp_1,
  output [3:0] hex_disp_0,
  output [31:0] COL_3,
  output [31:0] COL_3_2,
  output [31:0] COL_3_3,
  output [31:0] COL_3_4,
  output [31:0] COL_2,
  output [31:0] COL_2_2,
  output [31:0] COL_2_3,
  output [31:0] COL_2_4,
  output [31:0] COL_1,
  output [31:0] COL_1_2,
  output [31:0] COL_1_3,
  output [31:0] COL_1_4,
  output [31:0] COL_0,
  output [31:0] COL_0_2,
  output [31:0] COL_0_3,
  output [31:0] COL_0_4
);

  output_port_led_matrix_column_extender output_port_led_matrix_column_extender_1 (
    .matrix_column(COL_2), .port_column(PO[11:8]));
  output_port_led_matrix_column_extender output_port_led_matrix_column_extender_2 (
    .matrix_column(COL_1), .port_column(PO[7:4]));
  output_port_led_matrix_column_extender output_port_led_matrix_column_extender_3 (
    .matrix_column(COL_0), .port_column(PO[3:0]));
  output_port_led_matrix_column_extender output_port_led_matrix_column_extender_4 (
    .matrix_column(COL_3), .port_column(PO[15:12]));

  assign COL_0_2 = COL_0;
  assign COL_0_3 = COL_0;
  assign COL_0_4 = COL_0;
  assign COL_1_2 = COL_1;
  assign COL_1_3 = COL_1;
  assign COL_1_4 = COL_1;
  assign COL_2_2 = COL_2;
  assign COL_2_3 = COL_2;
  assign COL_2_4 = COL_2;
  assign COL_3_2 = COL_3;
  assign COL_3_3 = COL_3;
  assign COL_3_4 = COL_3;
  assign hex_disp_0 = PO[3:0];
  assign hex_disp_1 = PO[7:4];
  assign hex_disp_2 = PO[11:8];
  assign hex_disp_3 = PO[15:12];
endmodule

module output_port_led_matrix_column_extender (
  input  [3:0] port_column,
  output [31:0] matrix_column
);

  assign matrix_column[7:0] = {{7{port_column[0]}}, port_column[0]};  // Bit_Extender bit_extender_1
  assign matrix_column[15:8] = {{7{port_column[1]}}, port_column[1]};  // Bit_Extender bit_extender_2
  assign matrix_column[23:16] = {{7{port_column[2]}}, port_column[2]};  // Bit_Extender bit_extender_3
  assign matrix_column[31:24] = {{7{port_column[3]}}, port_column[3]};  // Bit_Extender bit_extender_4
endmodule

module stage2_status_viewer (
  input  is_free,
  input  is_done,
  output [15:0] out_3,
  output [15:0] out_4,
  output [15:0] out_5,
  output [15:0] out_6,
  output [15:0] out_7,
  output [15:0] out_8,
  output [15:0] out_9,
  output [15:0] out_10,
  output [15:0] out_11,
  output [15:0] out_12,
  output [15:0] out_13,
  output [15:0] out_14,
  output [15:0] out_15,
  output [15:0] out_16,
  output [15:0] out_17,
  output [15:0] out_18,
  output [15:0] out_19,
  output [15:0] out_20,
  output [15:0] out_21,
  output [15:0] out_22,
  output [15:0] out_23,
  output [15:0] out_24,
  output [15:0] out_25,
  output [15:0] out_26,
  output [15:0] out_27,
  output [15:0] out_28,
  output [15:0] out_29,
  output [15:0] out_30,
  output [15:0] out_31,
  output [15:0] out_32,
  output [15:0] out_33,
  output [15:0] out_34,
  output [15:0] out_35,
  output [15:0] out_36,
  output [15:0] out_37,
  output [15:0] out_38,
  output [15:0] out_39,
  output [15:0] out_40,
  output [15:0] out_41,
  output [15:0] out_42,
  output [15:0] out_43,
  output [15:0] out_44,
  output [15:0] out_45,
  output [15:0] out_46,
  output [15:0] out_47,
  output [15:0] out_48,
  output [15:0] out_49,
  output [15:0] out_50
);

  wire and_1_out, and_2_out, nor_1_out;

  and and_1 (and_1_out, is_free, ~is_done);  // AND_Gate
  nor nor_1 (nor_1_out, is_done, is_free);
  and and_2 (and_2_out, ~is_free, is_done);  // AND_Gate
  extender_1_to_16by16 extender_1_to_16by16_1 (
    .bit_to_extend(and_1_out), .out_2(out_3), .out_3(out_4), .out_4(out_5), .out_5(out_6), .out_6(out_7),
    .out_7(out_8), .out_8(out_9), .out_9(out_10), .out_10(out_11), .out_11(out_12), .out_12(out_13),
    .out_13(out_14), .out_14(out_15), .out_15(out_16), .out_16(out_17), .out_17(out_18));
  extender_1_to_16by16 extender_1_to_16by16_2 (
    .bit_to_extend(nor_1_out), .out_2(out_19), .out_3(out_20), .out_4(out_21), .out_5(out_22),
    .out_6(out_23), .out_7(out_24), .out_8(out_25), .out_9(out_26), .out_10(out_27), .out_11(out_28),
    .out_12(out_29), .out_13(out_30), .out_14(out_31), .out_15(out_32), .out_16(out_33), .out_17(out_34));
  extender_1_to_16by16 extender_1_to_16by16_3 (
    .bit_to_extend(and_2_out), .out_2(out_35), .out_3(out_36), .out_4(out_37), .out_5(out_38),
    .out_6(out_39), .out_7(out_40), .out_8(out_41), .out_9(out_42), .out_10(out_43), .out_11(out_44),
    .out_12(out_45), .out_13(out_46), .out_14(out_47), .out_15(out_48), .out_16(out_49), .out_17(out_50));
endmodule

module extender_1_to_16by16 (
  input  bit_to_extend,
  output [15:0] out_2,
  output [15:0] out_3,
  output [15:0] out_4,
  output [15:0] out_5,
  output [15:0] out_6,
  output [15:0] out_7,
  output [15:0] out_8,
  output [15:0] out_9,
  output [15:0] out_10,
  output [15:0] out_11,
  output [15:0] out_12,
  output [15:0] out_13,
  output [15:0] out_14,
  output [15:0] out_15,
  output [15:0] out_16,
  output [15:0] out_17
);

  assign out_2 = {{15{bit_to_extend}}, bit_to_extend};  // Bit_Extender bit_extender_1
  assign out_3 = {{15{bit_to_extend}}, bit_to_extend};  // Bit_Extender bit_extender_2
  assign out_4 = {{15{bit_to_extend}}, bit_to_extend};  // Bit_Extender bit_extender_3
  assign out_5 = {{15{bit_to_extend}}, bit_to_extend};  // Bit_Extender bit_extender_4
  assign out_6 = {{15{bit_to_extend}}, bit_to_extend};  // Bit_Extender bit_extender_5
  assign out_7 = {{15{bit_to_extend}}, bit_to_extend};  // Bit_Extender bit_extender_6
  assign out_8 = {{15{bit_to_extend}}, bit_to_extend};  // Bit_Extender bit_extender_7
  assign out_9 = {{15{bit_to_extend}}, bit_to_extend};  // Bit_Extender bit_extender_8
  assign out_10 = {{15{bit_to_extend}}, bit_to_extend};  // Bit_Extender bit_extender_9
  assign out_11 = {{15{bit_to_extend}}, bit_to_extend};  // Bit_Extender bit_extender_10
  assign out_12 = {{15{bit_to_extend}}, bit_to_extend};  // Bit_Extender bit_extender_11
  assign out_13 = {{15{bit_to_extend}}, bit_to_extend};  // Bit_Extender bit_extender_12
  assign out_14 = {{15{bit_to_extend}}, bit_to_extend};  // Bit_Extender bit_extender_13
  assign out_15 = {{15{bit_to_extend}}, bit_to_extend};  // Bit_Extender bit_extender_14
  assign out_16 = {{15{bit_to_extend}}, bit_to_extend};  // Bit_Extender bit_extender_15
  assign out_17 = {{15{bit_to_extend}}, bit_to_extend};  // Bit_Extender bit_extender_16
endmodule
